# Fritzing sketch arduino_exple (saved by Fritzing 0.9.0b)

parts:
  JP1 = Header 3 [package=screwterminal-3.5mm-3_lock.007s]
  Composant1 = Arduino Uno (Rev3)

nets:
  N1: JP1.1, Composant1.VIN
  N2: JP1.2, Composant1.D2
  N3: JP1.3, Composant1.GND

notes:
  signal
  +5VSB
  gnd
